// Logisim project Project (1).circ as structural Verilog
module register_file (
  input  [3:0] READ_1,
  input  [3:0] READ_2,
  input  [3:0] WRITE,
  input  [11:0] DATA,
  input  clk,
  input  Reg_write,
  input  def,
  output [11:0] READ_DATA_1,
  output [11:0] READ_DATA_2
);

  wire and_1_out, and_2_out, and_3_out, and_4_out, and_5_out, and_6_out, and_7_out, and_8_out, and_9_out,
       and_10_out, and_11_out, and_12_out, and_13_out, and_14_out, and_15_out, and_16_out, decoder_1_out0,
       decoder_1_out1, decoder_1_out2, decoder_1_out3, decoder_1_out4, decoder_1_out5, decoder_1_out6,
       decoder_1_out7, decoder_1_out8, decoder_1_out9, decoder_1_out10, decoder_1_out11, decoder_1_out12,
       decoder_1_out13, decoder_1_out14, decoder_1_out15;
  wire [11:0] multiplexer_2_out, R0_q, R1_def_q, R2_q, R3_q, R4_q, R5_q, R6_q, R7_q, R8_q, R9_q, R10_q,
       R11_q, R12_q, R13_q, R14_q, R15_q;

  Decoder #(.enable("false"), .select(4)) decoder_1 (
    .out0(decoder_1_out0), .out1(decoder_1_out1), .out2(decoder_1_out2), .out3(decoder_1_out3),
    .out4(decoder_1_out4), .out5(decoder_1_out5), .out6(decoder_1_out6), .out7(decoder_1_out7),
    .out8(decoder_1_out8), .out9(decoder_1_out9), .out10(decoder_1_out10), .out11(decoder_1_out11),
    .out12(decoder_1_out12), .out13(decoder_1_out13), .out14(decoder_1_out14), .out15(decoder_1_out15),
    .sel(WRITE));
  and and_1 (and_1_out, Reg_write, decoder_1_out0);
  and and_2 (and_2_out, Reg_write, decoder_1_out1);
  and and_3 (and_3_out, Reg_write, decoder_1_out2);
  and and_4 (and_4_out, Reg_write, decoder_1_out3);
  and and_5 (and_5_out, Reg_write, decoder_1_out4);
  and and_6 (and_6_out, Reg_write, decoder_1_out5);
  and and_7 (and_7_out, Reg_write, decoder_1_out6);
  and and_8 (and_8_out, Reg_write, decoder_1_out7);
  and and_9 (and_9_out, Reg_write, decoder_1_out8);
  and and_10 (and_10_out, Reg_write, decoder_1_out9);
  and and_11 (and_11_out, Reg_write, decoder_1_out10);
  and and_12 (and_12_out, Reg_write, decoder_1_out11);
  and and_13 (and_13_out, Reg_write, decoder_1_out12);
  and and_14 (and_14_out, Reg_write, decoder_1_out13);
  and and_15 (and_15_out, Reg_write, decoder_1_out14);
  and and_16 (and_16_out, Reg_write, decoder_1_out15);
  Register #(.width(12)) R0 (.D({12{1'b0}}), .en(and_1_out), .Q(R0_q), .clk(clk));  // open: clr
  Register #(.width(12)) R1_def (.D(DATA), .en(and_2_out), .Q(R1_def_q), .clk(clk));  // open: clr
  Register #(.width(12)) R2 (.D(DATA), .en(and_3_out), .Q(R2_q), .clk(clk));  // open: clr
  Register #(.width(12)) R3 (.D(DATA), .en(and_4_out), .Q(R3_q), .clk(clk));  // open: clr
  Register #(.width(12)) R4 (.D(DATA), .en(and_5_out), .Q(R4_q), .clk(clk));  // open: clr
  Register #(.width(12)) R5 (.D(DATA), .en(and_6_out), .Q(R5_q), .clk(clk));  // open: clr
  Register #(.width(12)) R6 (.D(DATA), .en(and_7_out), .Q(R6_q), .clk(clk));  // open: clr
  Register #(.width(12)) R7 (.D(DATA), .en(and_8_out), .Q(R7_q), .clk(clk));  // open: clr
  Register #(.width(12)) R8 (.D(DATA), .en(and_9_out), .Q(R8_q), .clk(clk));  // open: clr
  Register #(.width(12)) R9 (.D(DATA), .en(and_10_out), .Q(R9_q), .clk(clk));  // open: clr
  Register #(.width(12)) R10 (.D(DATA), .en(and_11_out), .Q(R10_q), .clk(clk));  // open: clr
  Register #(.width(12)) R11 (.D(DATA), .en(and_12_out), .Q(R11_q), .clk(clk));  // open: clr
  Register #(.width(12)) R12 (.D(DATA), .en(and_13_out), .Q(R12_q), .clk(clk));  // open: clr
  Register #(.width(12)) R13 (.D(DATA), .en(and_14_out), .Q(R13_q), .clk(clk));  // open: clr
  Register #(.width(12)) R14 (.D(DATA), .en(and_15_out), .Q(R14_q), .clk(clk));  // open: clr
  Register #(.width(12)) R15 (.D(DATA), .en(and_16_out), .Q(R15_q), .clk(clk));  // open: clr
  Multiplexer #(.select(4), .width(12)) multiplexer_1 (
    .in0(R0_q), .in1(R1_def_q), .in2(R2_q), .in3(R3_q), .in4(R4_q), .in5(R5_q), .in6(R6_q), .in7(R7_q),
    .in8(R8_q), .in9(R9_q), .in10(R10_q), .in11(R11_q), .in12(R12_q), .in13(R13_q), .in14(R14_q),
    .in15(R15_q), .out(READ_DATA_1), .sel(READ_1));
  Multiplexer #(.select(4), .width(12)) multiplexer_2 (
    .in0(R0_q), .in1(R1_def_q), .in2(R2_q), .in3(R3_q), .in4(R4_q), .in5(R5_q), .in6(R6_q), .in7(R7_q),
    .in8(R8_q), .in9(R9_q), .in10(R10_q), .in11(R11_q), .in12(R12_q), .in13(R13_q), .in14(R14_q),
    .in15(R15_q), .out(multiplexer_2_out), .sel(READ_2));
  Multiplexer #(.width(12)) multiplexer_3 (.in0(multiplexer_2_out), .in1(R1_def_q), .out(READ_DATA_2), .sel(def));
endmodule

module ALU_for_1bit (
  input  cin,
  input  A,
  input  B,
  input  Binv,
  input  [2:0] ALUop,
  output R,
  output cout
);

  wire adder_1_out, and_1_out, multiplexer_1_out, nand_1_out, nor_1_out, not_1_out, or_1_out;

  Multiplexer multiplexer_1 (.in0(B), .in1(not_1_out), .out(multiplexer_1_out), .sel(Binv));
  not not_1 (not_1_out, B);
  and and_1 (and_1_out, A, multiplexer_1_out);
  or or_1 (or_1_out, A, multiplexer_1_out);
  Adder #(.width(1)) adder_1 (.a(A), .b(multiplexer_1_out), .out(adder_1_out), .cin(cin), .cout(cout));
  nand nand_1 (nand_1_out, A, multiplexer_1_out);
  nor nor_1 (nor_1_out, A, multiplexer_1_out);
  Multiplexer #(.select(3)) multiplexer_2 (
    .in0(and_1_out), .in1(or_1_out), .in2(adder_1_out), .in3(nand_1_out), .in4(nor_1_out), .out(R),
    .sel(ALUop));  // open: in5, in6, in7
endmodule

module ALU_FOR_12BIT_WITH_1BIT (
  input  BINV,
  input  CIN,
  input  [11:0] A,
  input  [2:0] ALUOP,
  input  [11:0] B,
  output [11:0] R,
  output neg,
  output ZERO,
  output OVERFLOW,
  output COUT
);

  wire alu_for_1bit_1_cout, alu_for_1bit_2_cout, alu_for_1bit_3_cout, alu_for_1bit_4_cout,
       alu_for_1bit_5_cout, alu_for_1bit_6_cout, alu_for_1bit_7_cout, alu_for_1bit_8_cout,
       alu_for_1bit_9_cout, alu_for_1bit_10_cout, alu_for_1bit_11_cout;

  ALU_for_1bit alu_for_1bit_1 (
    .B(B[0]), .Binv(BINV), .A(A[0]), .cin(CIN), .ALUop(ALUOP), .cout(alu_for_1bit_1_cout), .R(R[0]));
  ALU_for_1bit alu_for_1bit_2 (
    .B(B[1]), .Binv(BINV), .A(A[1]), .cin(alu_for_1bit_1_cout), .ALUop(ALUOP), .cout(alu_for_1bit_2_cout),
    .R(R[1]));
  ALU_for_1bit alu_for_1bit_3 (
    .B(B[2]), .Binv(BINV), .A(A[2]), .cin(alu_for_1bit_2_cout), .ALUop(ALUOP), .cout(alu_for_1bit_3_cout),
    .R(R[2]));
  ALU_for_1bit alu_for_1bit_4 (
    .B(B[3]), .Binv(BINV), .A(A[3]), .cin(alu_for_1bit_3_cout), .ALUop(ALUOP), .cout(alu_for_1bit_4_cout),
    .R(R[3]));
  ALU_for_1bit alu_for_1bit_5 (
    .B(B[4]), .Binv(BINV), .A(A[4]), .cin(alu_for_1bit_4_cout), .ALUop(ALUOP), .cout(alu_for_1bit_5_cout),
    .R(R[4]));
  ALU_for_1bit alu_for_1bit_6 (
    .B(B[5]), .Binv(BINV), .A(A[5]), .cin(alu_for_1bit_5_cout), .ALUop(ALUOP), .cout(alu_for_1bit_6_cout),
    .R(R[5]));
  ALU_for_1bit alu_for_1bit_7 (
    .B(B[6]), .Binv(BINV), .A(A[6]), .cin(alu_for_1bit_6_cout), .ALUop(ALUOP), .cout(alu_for_1bit_7_cout),
    .R(R[6]));
  ALU_for_1bit alu_for_1bit_8 (
    .B(B[7]), .Binv(BINV), .A(A[7]), .cin(alu_for_1bit_7_cout), .ALUop(ALUOP), .cout(alu_for_1bit_8_cout),
    .R(R[7]));
  ALU_for_1bit alu_for_1bit_9 (
    .B(B[8]), .Binv(BINV), .A(A[8]), .cin(alu_for_1bit_8_cout), .ALUop(ALUOP), .cout(alu_for_1bit_9_cout),
    .R(R[8]));
  ALU_for_1bit alu_for_1bit_10 (
    .B(B[9]), .Binv(BINV), .A(A[9]), .cin(alu_for_1bit_9_cout), .ALUop(ALUOP), .cout(alu_for_1bit_10_cout),
    .R(R[9]));
  ALU_for_1bit alu_for_1bit_11 (
    .B(B[10]), .Binv(BINV), .A(A[10]), .cin(alu_for_1bit_10_cout), .ALUop(ALUOP),
    .cout(alu_for_1bit_11_cout), .R(R[10]));
  ALU_for_1bit alu_for_1bit_12 (
    .B(B[11]), .Binv(BINV), .A(A[11]), .cin(alu_for_1bit_11_cout), .ALUop(ALUOP), .cout(COUT), .R(neg));
  xor xor_1 (OVERFLOW, alu_for_1bit_11_cout, COUT);
  nor nor_1 (ZERO, R[0], R[1], R[2], R[3], R[4], R[5], R[6], R[7], R[8], R[9], R[10], neg);

  assign R[11] = neg;
endmodule

module Datapath (
  output [11:0] out_1,
  output [3:0] out_2,
  output [3:0] out_3,
  output [3:0] out_4,
  output [11:0] out_5,
  output [11:0] out_6,
  output [11:0] out_7,
  output [11:0] out_8
);

  wire alu_for_12bit_with_1bit_1_neg, alu_for_12bit_with_1bit_1_zero, and_1_out, and_2_out, clock_1_out,
       control01_1_beq, control01_1_binv, control01_1_bne, control01_1_cin, control01_1_def,
       control01_1_def_or_r, control01_1_j, control01_1_lw, control01_1_r_or_i, control01_1_reg_w,
       control01_1_sw, not_1_out, or_1_out;
  wire [2:0] control01_1_aluop, control01_1_mem_to_reg;
  wire [11:0] adder_1_out, adder_2_out, adder_3_out, bit_extender_1_out, bit_extender_2_out,
       multiplexer_1_out, multiplexer_2_out, multiplexer_3_out, multiplexer_4_out, multiplexer_5_out,
       register_1_q, register_file_1_read_data_1, register_file_1_read_data_2;

  Clock clock_1 (.out(clock_1_out));
  ROM #(.addrWidth(12), .dataWidth(12)) rom_1 (.addr(register_1_q), .data({out_4, out_3, out_2}));
  Register #(.width(12)) register_1 (.D(multiplexer_4_out), .Q(register_1_q), .clk(clock_1_out));  // open: en, clr
  Adder #(.width(12)) adder_1 (.a(register_1_q), .b(12'h1), .out(adder_1_out));  // open: cin, cout
  CONTROL01 control01_1 (
    .OPCODE(out_4), .REG_W(control01_1_reg_w), .DEF(control01_1_def), .R_OR_I(control01_1_r_or_i),
    .DEF_OR_R(control01_1_def_or_r), .BEQ(control01_1_beq), .BNE(control01_1_bne), .J(control01_1_j),
    .ALUOP(control01_1_aluop), .CIN(control01_1_cin), .BINV(control01_1_binv), .LW(control01_1_lw),
    .SW(control01_1_sw), .MEM_TO_REG(control01_1_mem_to_reg));
  register_file register_file_1 (
    .WRITE(out_3), .clk(clock_1_out), .Reg_write(control01_1_reg_w), .DATA(multiplexer_5_out),
    .READ_1(out_3), .READ_2(out_2), .def(control01_1_def), .READ_DATA_1(register_file_1_read_data_1),
    .READ_DATA_2(register_file_1_read_data_2));
  assign bit_extender_1_out = {{4{out_3[3]}}, {out_3, out_2}};  // Bit_Extender bit_extender_1
  Adder #(.width(12)) adder_2 (.a(bit_extender_2_out), .b(register_1_q), .out(adder_2_out));  // open: cin, cout
  assign bit_extender_2_out = {{8{1'b0}}, out_2};  // Bit_Extender bit_extender_2
  Multiplexer #(.width(12)) multiplexer_1 (
    .in0(adder_1_out), .in1(adder_2_out), .out(multiplexer_1_out), .sel(or_1_out));
  Multiplexer #(.width(12)) multiplexer_2 (
    .in0(register_file_1_read_data_1), .in1(register_file_1_read_data_2), .out(multiplexer_2_out),
    .sel(control01_1_def_or_r));
  Multiplexer #(.width(12)) multiplexer_3 (
    .in0(register_file_1_read_data_2), .in1(bit_extender_2_out), .out(multiplexer_3_out),
    .sel(control01_1_r_or_i));
  Adder #(.width(12)) adder_3 (.a(register_1_q), .b(bit_extender_1_out), .out(adder_3_out));  // open: cin, cout
  Shifter #(.width(12)) shifter_1 (.in(register_file_1_read_data_1), .\dist (out_2), .out(out_7));
  Shifter #(.shift("lr"), .width(12)) shifter_2 (.in(register_file_1_read_data_1), .\dist (out_2), .out(out_8));
  Multiplexer #(.width(12)) multiplexer_4 (
    .in0(multiplexer_1_out), .in1(adder_3_out), .out(multiplexer_4_out), .sel(control01_1_j));
  ALU_FOR_12BIT_WITH_1BIT alu_for_12bit_with_1bit_1 (
    .A(multiplexer_2_out), .B(multiplexer_3_out), .BINV(control01_1_binv), .CIN(control01_1_cin),
    .ALUOP(control01_1_aluop), .R(out_1), .neg(alu_for_12bit_with_1bit_1_neg),
    .ZERO(alu_for_12bit_with_1bit_1_zero));  // open: COUT, OVERFLOW
  and and_1 (and_1_out, control01_1_beq, alu_for_12bit_with_1bit_1_zero);
  not not_1 (not_1_out, alu_for_12bit_with_1bit_1_zero);
  and and_2 (and_2_out, not_1_out, control01_1_bne);
  RAM #(.addrWidth(12), .dataWidth(12)) ram_1 (
    .addr(out_1), .we(control01_1_sw), .oe(control01_1_lw), .clk(clock_1_out),
    .din(register_file_1_read_data_1), .dout(out_6));
  or or_1 (or_1_out, and_1_out, and_2_out);
  assign out_5 = {{11{1'b0}}, alu_for_12bit_with_1bit_1_neg};  // Bit_Extender bit_extender_3
  Multiplexer #(.select(3), .width(12)) multiplexer_5 (
    .in0(out_1), .in1(out_6), .in2(out_7), .in3(out_8), .in4(out_5), .out(multiplexer_5_out),
    .sel(control01_1_mem_to_reg));  // open: in5, in6, in7
endmodule

module CONTROL01 (
  input  [3:0] OPCODE,
  output REG_W,
  output DEF,
  output R_OR_I,
  output DEF_OR_R,
  output BEQ,
  output BNE,
  output J,
  output [2:0] ALUOP,
  output CIN,
  output BINV,
  output LW,
  output SW,
  output [2:0] MEM_TO_REG
);

  wire and_1_out, and_2_out, and_3_out, and_4_out, and_5_out, and_6_out, and_7_out, and_8_out, and_9_out,
       and_14_out, and_15_out, and_16_out, and_17_out, and_18_out, and_19_out, and_20_out, and_21_out,
       and_22_out, and_23_out, and_24_out, and_25_out, and_26_out, and_30_out, and_31_out, not_1_out,
       not_2_out, not_3_out, not_4_out;

  not not_1 (not_1_out, OPCODE[3]);
  not not_2 (not_2_out, OPCODE[2]);
  not not_3 (not_3_out, OPCODE[1]);
  not not_4 (not_4_out, OPCODE[0]);
  or or_1 (REG_W, not_1_out, OPCODE[2]);
  and and_1 (and_1_out, not_1_out, OPCODE[2], OPCODE[1], OPCODE[0]);
  and and_2 (and_2_out, OPCODE[3], not_2_out, not_3_out);
  and and_3 (and_3_out, OPCODE[3], not_2_out, not_4_out);
  and and_4 (and_4_out, not_1_out, not_3_out, OPCODE[0]);
  and and_5 (and_5_out, not_1_out, OPCODE[2], OPCODE[1]);
  and and_6 (and_6_out, OPCODE[3], not_2_out, not_3_out, not_4_out);
  and and_7 (and_7_out, OPCODE[2], not_3_out, OPCODE[0]);
  and and_8 (and_8_out, not_1_out, OPCODE[2], OPCODE[1], OPCODE[0]);
  and and_9 (and_9_out, OPCODE[3], not_2_out, not_3_out, not_4_out);
  and and_10 (BEQ, OPCODE[3], not_2_out, not_3_out, OPCODE[0]);
  and and_11 (BNE, OPCODE[3], not_2_out, OPCODE[1], not_4_out);
  and and_12 (J, OPCODE[3], not_2_out, OPCODE[1], OPCODE[0]);
  and and_13 (ALUOP[2], OPCODE[3], OPCODE[2], OPCODE[1], OPCODE[0]);
  and and_14 (and_14_out, not_2_out, not_3_out);
  and and_15 (and_15_out, not_2_out, not_4_out);
  and and_16 (and_16_out, not_1_out, OPCODE[2], OPCODE[1], OPCODE[0]);
  and and_17 (and_17_out, OPCODE[3], not_3_out);
  and and_18 (and_18_out, OPCODE[3], not_4_out);
  and and_19 (and_19_out, not_1_out, OPCODE[2], not_3_out, not_4_out);
  and and_20 (and_20_out, OPCODE[3], OPCODE[2], OPCODE[1], not_4_out);
  and and_21 (and_21_out, not_2_out, OPCODE[1], not_4_out);
  and and_22 (and_22_out, OPCODE[3], not_3_out, OPCODE[0]);
  and and_23 (and_23_out, OPCODE[3], OPCODE[2], not_3_out);
  and and_24 (and_24_out, not_2_out, OPCODE[1], not_4_out);
  and and_25 (and_25_out, OPCODE[3], not_3_out, OPCODE[0]);
  and and_26 (and_26_out, OPCODE[3], OPCODE[2], not_3_out);
  and and_27 (LW, not_1_out, OPCODE[2], OPCODE[1], OPCODE[0]);
  and and_28 (SW, OPCODE[3], not_2_out, not_3_out, not_4_out);
  and and_29 (MEM_TO_REG[2], OPCODE[3], OPCODE[2], not_3_out);
  and and_30 (and_30_out, not_1_out, OPCODE[2], not_3_out, OPCODE[0]);
  and and_31 (and_31_out, not_1_out, OPCODE[2], OPCODE[1], not_4_out);
  and and_32 (MEM_TO_REG[0], not_1_out, OPCODE[2], OPCODE[1]);
  or or_2 (DEF, and_1_out, and_2_out, and_3_out);
  or or_3 (R_OR_I, and_4_out, and_5_out, and_6_out, and_7_out);
  or or_4 (DEF_OR_R, and_8_out, and_9_out);
  or or_5 (ALUOP[1], and_14_out, and_15_out, and_16_out, and_17_out, and_18_out);
  or or_6 (ALUOP[0], and_19_out, and_20_out);
  or or_7 (CIN, and_21_out, and_22_out, and_23_out);
  or or_8 (BINV, and_24_out, and_25_out, and_26_out);
  or or_9 (MEM_TO_REG[1], and_30_out, and_31_out);
endmodule
