// Logisim project Project.circ as structural Verilog
module register_file (
  input  [3:0] READ_1,
  input  [3:0] READ_2,
  input  [3:0] WRITE,
  input  [11:0] DATA,
  input  clk,
  input  Reg_write,
  input  def,
  output [11:0] READ_DATA_1,
  output [11:0] READ_DATA_2
);

  wire and_1_out, and_2_out, and_3_out, and_4_out, and_5_out, and_6_out, and_7_out, and_8_out, and_9_out,
       and_10_out, and_11_out, and_12_out, and_13_out, and_14_out, and_15_out, and_16_out, decoder_1_out0,
       decoder_1_out1, decoder_1_out2, decoder_1_out3, decoder_1_out4, decoder_1_out5, decoder_1_out6,
       decoder_1_out7, decoder_1_out8, decoder_1_out9, decoder_1_out10, decoder_1_out11, decoder_1_out12,
       decoder_1_out13, decoder_1_out14, decoder_1_out15;
  wire [11:0] multiplexer_2_out, R0_q, R1_def_q, R2_q, R3_q, R4_q, R5_q, R6_q, R7_q, R8_q, R9_q, R10_q,
       R11_q, R12_q, R13_q, R14_q, R15_q;

  Decoder #(.enable("false"), .select(4)) decoder_1 (
    .out0(decoder_1_out0), .out1(decoder_1_out1), .out2(decoder_1_out2), .out3(decoder_1_out3),
    .out4(decoder_1_out4), .out5(decoder_1_out5), .out6(decoder_1_out6), .out7(decoder_1_out7),
    .out8(decoder_1_out8), .out9(decoder_1_out9), .out10(decoder_1_out10), .out11(decoder_1_out11),
    .out12(decoder_1_out12), .out13(decoder_1_out13), .out14(decoder_1_out14), .out15(decoder_1_out15),
    .sel(WRITE));
  and and_1 (and_1_out, Reg_write, decoder_1_out0);
  and and_2 (and_2_out, Reg_write, decoder_1_out1);
  and and_3 (and_3_out, Reg_write, decoder_1_out2);
  and and_4 (and_4_out, Reg_write, decoder_1_out3);
  and and_5 (and_5_out, Reg_write, decoder_1_out4);
  and and_6 (and_6_out, Reg_write, decoder_1_out5);
  and and_7 (and_7_out, Reg_write, decoder_1_out6);
  and and_8 (and_8_out, Reg_write, decoder_1_out7);
  and and_9 (and_9_out, Reg_write, decoder_1_out8);
  and and_10 (and_10_out, Reg_write, decoder_1_out9);
  and and_11 (and_11_out, Reg_write, decoder_1_out10);
  and and_12 (and_12_out, Reg_write, decoder_1_out11);
  and and_13 (and_13_out, Reg_write, decoder_1_out12);
  and and_14 (and_14_out, Reg_write, decoder_1_out13);
  and and_15 (and_15_out, Reg_write, decoder_1_out14);
  and and_16 (and_16_out, Reg_write, decoder_1_out15);
  Register #(.width(12)) R0 (.D({12{1'b0}}), .en(and_1_out), .Q(R0_q), .clk(clk));  // open: clr
  Register #(.width(12)) R1_def (.D(DATA), .en(and_2_out), .Q(R1_def_q), .clk(clk));  // open: clr
  Register #(.width(12)) R2 (.D(DATA), .en(and_3_out), .Q(R2_q), .clk(clk));  // open: clr
  Register #(.width(12)) R3 (.D(DATA), .en(and_4_out), .Q(R3_q), .clk(clk));  // open: clr
  Register #(.width(12)) R4 (.D(DATA), .en(and_5_out), .Q(R4_q), .clk(clk));  // open: clr
  Register #(.width(12)) R5 (.D(DATA), .en(and_6_out), .Q(R5_q), .clk(clk));  // open: clr
  Register #(.width(12)) R6 (.D(DATA), .en(and_7_out), .Q(R6_q), .clk(clk));  // open: clr
  Register #(.width(12)) R7 (.D(DATA), .en(and_8_out), .Q(R7_q), .clk(clk));  // open: clr
  Register #(.width(12)) R8 (.D(DATA), .en(and_9_out), .Q(R8_q), .clk(clk));  // open: clr
  Register #(.width(12)) R9 (.D(DATA), .en(and_10_out), .Q(R9_q), .clk(clk));  // open: clr
  Register #(.width(12)) R10 (.D(DATA), .en(and_11_out), .Q(R10_q), .clk(clk));  // open: clr
  Register #(.width(12)) R11 (.D(DATA), .en(and_12_out), .Q(R11_q), .clk(clk));  // open: clr
  Register #(.width(12)) R12 (.D(DATA), .en(and_13_out), .Q(R12_q), .clk(clk));  // open: clr
  Register #(.width(12)) R13 (.D(DATA), .en(and_14_out), .Q(R13_q), .clk(clk));  // open: clr
  Register #(.width(12)) R14 (.D(DATA), .en(and_15_out), .Q(R14_q), .clk(clk));  // open: clr
  Register #(.width(12)) R15 (.D(DATA), .en(and_16_out), .Q(R15_q), .clk(clk));  // open: clr
  Multiplexer #(.select(4), .width(12)) multiplexer_1 (
    .in0(R0_q), .in1(R1_def_q), .in2(R2_q), .in3(R3_q), .in4(R4_q), .in5(R5_q), .in6(R6_q), .in7(R7_q),
    .in8(R8_q), .in9(R9_q), .in10(R10_q), .in11(R11_q), .in12(R12_q), .in13(R13_q), .in14(R14_q),
    .in15(R15_q), .out(READ_DATA_1), .sel(READ_1));
  Multiplexer #(.select(4), .width(12)) multiplexer_2 (
    .in0(R0_q), .in1(R1_def_q), .in2(R2_q), .in3(R3_q), .in4(R4_q), .in5(R5_q), .in6(R6_q), .in7(R7_q),
    .in8(R8_q), .in9(R9_q), .in10(R10_q), .in11(R11_q), .in12(R12_q), .in13(R13_q), .in14(R14_q),
    .in15(R15_q), .out(multiplexer_2_out), .sel(READ_2));
  Multiplexer #(.width(12)) multiplexer_3 (.in0(multiplexer_2_out), .in1(R1_def_q), .out(READ_DATA_2), .sel(def));
endmodule

module ALU_for_1bit (
  input  cin,
  input  A,
  input  [2:0] ALUop,
  input  B,
  input  Binv,
  output R,
  output cout
);

  wire adder_1_out, and_1_out, multiplexer_1_out, not_1_out, or_1_out;

  Multiplexer multiplexer_1 (.in0(B), .in1(not_1_out), .out(multiplexer_1_out), .sel(Binv));
  not not_1 (not_1_out, B);
  and and_1 (and_1_out, A, multiplexer_1_out);
  or or_1 (or_1_out, A, multiplexer_1_out);
  Adder #(.width(1)) adder_1 (.a(A), .b(multiplexer_1_out), .out(adder_1_out), .cin(cin), .cout(cout));
  Multiplexer #(.select(3)) multiplexer_2 (
    .in0(and_1_out), .in1(or_1_out), .in2(adder_1_out), .out(R), .sel(ALUop));  // open: in3, in4, in5, in6, in7
endmodule

module ALU_FOR_12BIT_WITH_1BIT (
  input  BINV,
  input  CIN,
  input  [11:0] A,
  input  [2:0] ALUOP,
  input  [11:0] B,
  output [11:0] R,
  output neg,
  output ZERO,
  output OVERFLOW,
  output COUT
);

  wire alu_for_1bit_1_cout, alu_for_1bit_2_cout, alu_for_1bit_3_cout, alu_for_1bit_4_cout,
       alu_for_1bit_5_cout, alu_for_1bit_6_cout, alu_for_1bit_7_cout, alu_for_1bit_8_cout,
       alu_for_1bit_9_cout, alu_for_1bit_10_cout, alu_for_1bit_11_cout;

  ALU_for_1bit alu_for_1bit_1 (
    .B(B[0]), .Binv(BINV), .A(A[0]), .cin(CIN), .ALUop(ALUOP), .cout(alu_for_1bit_1_cout), .R(R[0]));
  ALU_for_1bit alu_for_1bit_2 (
    .B(B[1]), .Binv(BINV), .A(A[1]), .cin(alu_for_1bit_1_cout), .ALUop(ALUOP), .cout(alu_for_1bit_2_cout),
    .R(R[1]));
  ALU_for_1bit alu_for_1bit_3 (
    .B(B[2]), .Binv(BINV), .A(A[2]), .cin(alu_for_1bit_2_cout), .ALUop(ALUOP), .cout(alu_for_1bit_3_cout),
    .R(R[2]));
  ALU_for_1bit alu_for_1bit_4 (
    .B(B[3]), .Binv(BINV), .A(A[3]), .cin(alu_for_1bit_3_cout), .ALUop(ALUOP), .cout(alu_for_1bit_4_cout),
    .R(R[3]));
  ALU_for_1bit alu_for_1bit_5 (
    .B(B[4]), .Binv(BINV), .A(A[4]), .cin(alu_for_1bit_4_cout), .ALUop(ALUOP), .cout(alu_for_1bit_5_cout),
    .R(R[4]));
  ALU_for_1bit alu_for_1bit_6 (
    .B(B[5]), .Binv(BINV), .A(A[5]), .cin(alu_for_1bit_5_cout), .ALUop(ALUOP), .cout(alu_for_1bit_6_cout),
    .R(R[5]));
  ALU_for_1bit alu_for_1bit_7 (
    .B(B[6]), .Binv(BINV), .A(A[6]), .cin(alu_for_1bit_6_cout), .ALUop(ALUOP), .cout(alu_for_1bit_7_cout),
    .R(R[6]));
  ALU_for_1bit alu_for_1bit_8 (
    .B(B[7]), .Binv(BINV), .A(A[7]), .cin(alu_for_1bit_7_cout), .ALUop(ALUOP), .cout(alu_for_1bit_8_cout),
    .R(R[7]));
  ALU_for_1bit alu_for_1bit_9 (
    .B(B[8]), .Binv(BINV), .A(A[8]), .cin(alu_for_1bit_8_cout), .ALUop(ALUOP), .cout(alu_for_1bit_9_cout),
    .R(R[8]));
  ALU_for_1bit alu_for_1bit_10 (
    .B(B[9]), .Binv(BINV), .A(A[9]), .cin(alu_for_1bit_9_cout), .ALUop(ALUOP), .cout(alu_for_1bit_10_cout),
    .R(R[9]));
  ALU_for_1bit alu_for_1bit_11 (
    .B(B[10]), .Binv(BINV), .A(A[10]), .cin(alu_for_1bit_10_cout), .ALUop(ALUOP),
    .cout(alu_for_1bit_11_cout), .R(R[10]));
  ALU_for_1bit alu_for_1bit_12 (
    .B(B[11]), .Binv(BINV), .A(A[11]), .cin(alu_for_1bit_11_cout), .ALUop(ALUOP), .cout(COUT), .R(neg));
  xor xor_1 (OVERFLOW, alu_for_1bit_11_cout, COUT);
  nor nor_1 (ZERO, R[0], R[1], R[2], R[3], R[4], R[5], R[6], R[7], R[8], R[9], R[10], neg);

  assign R[11] = neg;
endmodule

module Datapath (
  output [3:0] out_1,
  output [3:0] out_2,
  output [3:0] out_3
);

  wire alu_for_12bit_with_1bit_1_neg, alu_for_12bit_with_1bit_1_zero, and_1_out, and_2_out, clock_1_out,
       control_1_alu_src, control_1_beq, control_1_binv, control_1_bne, control_1_cin, control_1_def,
       control_1_jump, control_1_lw, control_1_reg_w, control_1_sw, not_1_out, or_1_out;
  wire [2:0] control_1_aluop, control_1_mem_to_reg;
  wire [11:0] adder_1_out, adder_2_out, adder_3_out, alu_for_12bit_with_1bit_1_r, bit_extender_1_out,
       bit_extender_2_out, bit_extender_3_out, multiplexer_1_out, multiplexer_2_out, multiplexer_3_out,
       multiplexer_4_out, ram_1_dout, register_1_q, register_file_1_read_data_1, register_file_1_read_data_2,
       shifter_1_out, shifter_2_out;

  Clock clock_1 (.out(clock_1_out));
  ROM #(.addrWidth(12), .dataWidth(12)) rom_1 (.addr(register_1_q), .data({out_3, out_2, out_1}));
  Register #(.width(12)) register_1 (.D(multiplexer_3_out), .Q(register_1_q), .clk(clock_1_out));  // open: en, clr
  Adder #(.width(12)) adder_1 (.a(register_1_q), .b(12'h1), .out(adder_1_out));  // open: cin, cout
  control control_1 (
    .opcode(out_3), .reg_w(control_1_reg_w), .def(control_1_def), .alu_src(control_1_alu_src),
    .aluop(control_1_aluop), .cin(control_1_cin), .binv(control_1_binv), .beq(control_1_beq),
    .bne(control_1_bne), .jump(control_1_jump), .mem_to_reg(control_1_mem_to_reg), .lw(control_1_lw),
    .sw(control_1_sw));
  register_file register_file_1 (
    .WRITE(out_2), .clk(clock_1_out), .Reg_write(control_1_reg_w), .DATA(multiplexer_4_out), .READ_1(out_2),
    .READ_2(out_1), .def(control_1_def), .READ_DATA_1(register_file_1_read_data_1),
    .READ_DATA_2(register_file_1_read_data_2));
  assign bit_extender_1_out = {{4{out_1[3]}}, {out_1, out_2}};  // Bit_Extender bit_extender_1
  Adder #(.width(12)) adder_2 (.a(adder_1_out), .b(bit_extender_2_out), .out(adder_2_out));  // open: cin, cout
  assign bit_extender_2_out = {{8{out_1[3]}}, out_1};  // Bit_Extender bit_extender_2
  Multiplexer #(.width(12)) multiplexer_1 (
    .in0(adder_1_out), .in1(adder_2_out), .out(multiplexer_1_out), .sel(or_1_out));
  Multiplexer #(.width(12)) multiplexer_2 (
    .in0(register_file_1_read_data_2), .in1(bit_extender_2_out), .out(multiplexer_2_out),
    .sel(control_1_alu_src));
  Adder #(.width(12)) adder_3 (.a(multiplexer_1_out), .b(bit_extender_1_out), .out(adder_3_out));  // open: cin, cout
  Shifter #(.width(12)) shifter_1 (.in(register_file_1_read_data_1), .\dist (out_1), .out(shifter_1_out));
  Shifter #(.shift("lr"), .width(12)) shifter_2 (.in(register_file_1_read_data_1), .\dist (out_1), .out(shifter_2_out));
  Multiplexer #(.width(12)) multiplexer_3 (
    .in0(multiplexer_1_out), .in1(adder_3_out), .out(multiplexer_3_out), .sel(control_1_jump));
  ALU_FOR_12BIT_WITH_1BIT alu_for_12bit_with_1bit_1 (
    .A(register_file_1_read_data_1), .B(multiplexer_2_out), .BINV(control_1_binv), .CIN(control_1_cin),
    .ALUOP(control_1_aluop), .R(alu_for_12bit_with_1bit_1_r), .neg(alu_for_12bit_with_1bit_1_neg),
    .ZERO(alu_for_12bit_with_1bit_1_zero));  // open: COUT, OVERFLOW
  and and_1 (and_1_out, control_1_beq, alu_for_12bit_with_1bit_1_zero);
  not not_1 (not_1_out, alu_for_12bit_with_1bit_1_zero);
  and and_2 (and_2_out, control_1_bne, not_1_out);
  RAM #(.addrWidth(12), .dataWidth(12)) ram_1 (
    .addr(alu_for_12bit_with_1bit_1_r), .we(control_1_sw), .oe(control_1_lw), .clk(clock_1_out),
    .din(register_file_1_read_data_2), .dout(ram_1_dout));
  or or_1 (or_1_out, and_1_out, and_2_out);
  assign bit_extender_3_out = {{11{alu_for_12bit_with_1bit_1_neg}}, alu_for_12bit_with_1bit_1_neg};  // Bit_Extender bit_extender_3
  Multiplexer #(.select(3), .width(12)) multiplexer_4 (
    .in0(alu_for_12bit_with_1bit_1_r), .in1(ram_1_dout), .in2(shifter_1_out), .in3(shifter_2_out),
    .in4(bit_extender_3_out), .out(multiplexer_4_out), .sel(control_1_mem_to_reg));  // open: in5, in6, in7

  // Notes on the sheet:
  //   contents of rom_1 (hex, n*v repeats v):
  //   922
endmodule

module control (
  input  [3:0] opcode,
  output reg_w,
  output def,
  output alu_src,
  output [2:0] aluop,
  output cin,
  output binv,
  output beq,
  output bne,
  output jump,
  output [2:0] mem_to_reg,
  output lw,
  output sw
);

  wire and_1_out, and_2_out, and_3_out, and_4_out, and_5_out, and_6_out, and_7_out, and_8_out, and_9_out,
       and_10_out, and_11_out, and_13_out, and_14_out, and_15_out, and_16_out, and_17_out, and_18_out,
       and_23_out, and_24_out, not_1_out, not_2_out, not_3_out, not_4_out;

  not not_1 (not_1_out, opcode[3]);
  not not_2 (not_2_out, opcode[2]);
  not not_3 (not_3_out, opcode[1]);
  not not_4 (not_4_out, opcode[0]);
  and and_1 (and_1_out, opcode[2], not_3_out);
  and and_2 (and_2_out, not_1_out, opcode[2], opcode[1], opcode[0]);
  and and_3 (and_3_out, opcode[3], not_2_out, not_3_out);
  and and_4 (and_4_out, opcode[3], not_2_out, not_4_out);
  and and_5 (and_5_out, not_3_out, opcode[0]);
  and and_6 (and_6_out, opcode[2], opcode[1]);
  and and_7 (and_7_out, opcode[3], not_2_out, not_4_out);
  and and_8 (and_8_out, not_2_out, not_3_out);
  and and_9 (and_9_out, not_2_out, not_4_out);
  and and_10 (and_10_out, not_1_out, opcode[2], opcode[1], opcode[0]);
  and and_11 (and_11_out, opcode[3], not_3_out);
  and and_12 (aluop[0], not_1_out, opcode[2], not_3_out, not_4_out);
  and and_13 (and_13_out, not_2_out, opcode[1], not_4_out);
  and and_14 (and_14_out, opcode[3], not_3_out, opcode[0]);
  and and_15 (and_15_out, opcode[3], opcode[2], not_3_out);
  and and_16 (and_16_out, not_2_out, opcode[1], not_4_out);
  and and_17 (and_17_out, opcode[3], not_3_out, opcode[0]);
  and and_18 (and_18_out, opcode[3], opcode[2], not_3_out);
  and and_19 (beq, opcode[3], not_2_out, not_3_out, opcode[0]);
  and and_20 (bne, opcode[3], not_2_out, opcode[1], not_4_out);
  and and_21 (jump, opcode[3], not_2_out, opcode[1], opcode[0]);
  and and_22 (mem_to_reg[2], opcode[3], opcode[2], not_3_out);
  and and_23 (and_23_out, not_1_out, opcode[2], not_3_out, opcode[0]);
  and and_24 (and_24_out, not_1_out, opcode[2], opcode[1], not_4_out);
  and and_25 (mem_to_reg[0], not_1_out, opcode[2], opcode[1], not_4_out);
  and and_26 (lw, not_1_out, opcode[2], opcode[1], opcode[0]);
  and and_27 (sw, opcode[3], not_2_out, not_3_out, not_4_out);
  or or_1 (reg_w, not_1_out, and_1_out);
  or or_2 (def, and_2_out, and_3_out, and_4_out);
  or or_3 (alu_src, and_5_out, and_6_out, and_7_out);
  or or_4 (aluop[1], and_8_out, and_9_out, and_10_out, and_11_out);
  or or_5 (cin, and_13_out, and_14_out, and_15_out);
  or or_6 (binv, and_16_out, and_17_out, and_18_out);
  or or_7 (mem_to_reg[1], and_23_out, and_24_out);

  assign aluop[2] = 1'b0;
endmodule
